// Logisim project cjm235_proj2.circ as structural Verilog: 6 circuits, main circuit main
module main (
);

  wire ALUBSrc, BranchOp, button_1_out, CK, clock_1_out, DispWE, hlt, Jr, Jump, MemWE, RegWE;
  wire [1:0] Branch;
  wire [2:0] ALUOP, rd, RegDataSrc, rs, rt;
  wire [3:0] display_1_out_4, display_1_out_5, display_1_out_6, display_1_out_7;
  wire [7:0] pc_fsm_1_pc_out;
  wire [15:0] ALU, Imm, multiplexer_2_out, multiplexer_3_out, PC_1, RAM, Reg_rs, Reg_rt, shifter_1_out,
       target;
  wire [21:0] rom_1_data;

  Clock clock_1 (.out(clock_1_out));
  or or_1 (CK, clock_1_out, button_1_out);
  Button button_1 (.out(button_1_out));
  Hex_Digit_Display hex_digit_display_1 (.value(display_1_out_4));  // open: dp
  Display display_1 (
    .WE(DispWE), .Data(Reg_rs), .out_4(display_1_out_4), .out_5(display_1_out_5), .out_6(display_1_out_6),
    .out_7(display_1_out_7), .CLK(CK));
  Hex_Digit_Display hex_digit_display_2 (.value(display_1_out_5));  // open: dp
  Hex_Digit_Display hex_digit_display_3 (.value(display_1_out_6));  // open: dp
  PC_FSM pc_fsm_1 (
    .CLK(CK), .Offset(Imm), .Target(target), .Jump(Jump), .Branch(Branch), .Halt(hlt),
    .PC_Out(pc_fsm_1_pc_out), .PC_1_Out(PC_1), .Reg_rs(Reg_rs), .Reg_rt(Reg_rt), .isBranch(BranchOp));
  Hex_Digit_Display hex_digit_display_4 (.value(display_1_out_7));  // open: dp
  LED HALT (.in(hlt));
  // Probe on pc_fsm_1_pc_out
  ROM #(.dataWidth(22)) rom_1 (.addr(pc_fsm_1_pc_out), .data(rom_1_data));  // open: sel
  Multiplexer #(.width(16)) multiplexer_1 (.in0(Imm), .in1(Reg_rs), .out(target), .sel(Jr));  // open: en
  RAM #(.addrWidth(16), .dataWidth(16), .bus("separate")) ram_1 (
    .addr(ALU), .din(Reg_rt), .data(RAM), .str(MemWE), .clk(CK));  // open: sel, ld, clr
  Multiplexer #(.width(16)) multiplexer_2 (
    .in0(Reg_rt), .in1(Imm), .out(multiplexer_2_out), .sel(ALUBSrc));  // open: en
  Shifter #(.width(16)) shifter_1 (.in(Imm), .\dist (4'b1000), .out(shifter_1_out));
  Control Control (
    .Instruction(rom_1_data), .rd(rd), .rs(rs), .rt(rt), .hlt(hlt), .RegWE(RegWE), .MemWE(MemWE),
    .DispWE(DispWE), .RegDataSrc(RegDataSrc), .imm(Imm), .ALUBSrc(ALUBSrc), .ALUOP(ALUOP), .Jump(Jump),
    .is_Branch(BranchOp), .jr(Jr), .BranchOp(Branch));
  ALU alu_1 (.A(Reg_rs), .B(multiplexer_2_out), .ALU_Op(ALUOP), .ALU_Out(ALU));
  Multiplexer #(.select(3), .width(16)) multiplexer_3 (
    .in0(ALU), .in1(Imm), .in2(shifter_1_out), .in3(RAM), .in4(PC_1), .out(multiplexer_3_out),
    .sel(RegDataSrc));  // open: in5, in6, in7, en
  Register_File register_file_1 (
    .REG_rd(multiplexer_3_out), .rd(rd), .Reg_WE(RegWE), .rs(rs), .rt(rt), .CLK(CK), .REG_rs(Reg_rs),
    .REG_rt(Reg_rt));

  // Notes on the sheet:
  //   contents of rom_1 (hex, n*v repeats v):
  //   40240 20008 1e0248 2c0200
endmodule

module Display (
  input  CLK,
  input  WE,
  input  [15:0] Data,
  output [3:0] out_4,
  output [3:0] out_5,
  output [3:0] out_6,
  output [3:0] out_7
);

  Register #(.width(16)) register_1 (.D(Data), .en(WE), .Q({out_4, out_5, out_6, out_7}), .clk(CLK));  // open: clr

  // Other names for the same wires on the sheet: Digit_4[3:0] = out_7; Digt_3[3:0] = out_6; Digit_2[3:0] = out_5;
  //   Digit_1[3:0] = out_4
endmodule

module ALU (
  input  [15:0] A,
  input  [15:0] B,
  input  [2:0] ALU_Op,
  output [15:0] ALU_Out
);

  wire [3:0] bit_extender_1_out;
  wire [15:0] adder_1_out, and_1_out, not_1_p2, or_1_out, shifter_1_out, shifter_2_out, subtractor_1_out,
       undriven, xor_1_out;

  Bit_Extender #(.in_width(16), .out_width(4)) bit_extender_1 (.in(B), .out(bit_extender_1_out));
  Adder #(.width(16)) adder_1 (.a(A), .b(B), .out(adder_1_out));  // open: cin, cout
  Subtractor #(.width(16)) subtractor_1 (.a(A), .b(B), .out(subtractor_1_out));  // open: bin, bout
  assign and_1_out = A & B & undriven;  // AND_Gate and_1, 16 bits wide
  assign or_1_out = undriven | A | B;  // OR_Gate or_1, 16 bits wide
  assign xor_1_out = A ^ B;  // XOR_Gate xor_1, 16 bits wide
  // NOT_Gate #(.width(16)) not_1: pin names not known; wires that end beside it: B, not_1_p2
  Shifter #(.width(16)) shifter_1 (.in(A), .\dist (bit_extender_1_out), .out(shifter_1_out));
  Shifter #(.width(16), .shift("lr")) shifter_2 (.in(A), .\dist (bit_extender_1_out), .out(shifter_2_out));
  Multiplexer #(.select(3), .width(16)) multiplexer_1 (
    .in0(adder_1_out), .in1(subtractor_1_out), .in2(and_1_out), .in3(or_1_out), .in4(xor_1_out),
    .in5(not_1_p2), .in6(shifter_1_out), .in7(shifter_2_out), .out(ALU_Out), .sel(ALU_Op));  // open: en
endmodule

// Register
module Register_File (
  input  [15:0] REG_rd,
  input  [2:0] rd,
  input  Reg_WE,
  input  [2:0] rs,
  input  [2:0] rt,
  input  CLK,
  output [15:0] REG_rs,
  output [15:0] REG_rt
);

  wire demultiplexer_1_out0, demultiplexer_1_out1, demultiplexer_1_out2, demultiplexer_1_out3,
       demultiplexer_1_out4, demultiplexer_1_out5, demultiplexer_1_out6, demultiplexer_1_out7;
  wire [15:0] register_1_q, register_2_q, register_3_q, register_4_q, register_5_q, register_6_q,
       register_7_q;

  Demultiplexer #(.select(3)) demultiplexer_1 (
    .out0(demultiplexer_1_out0), .out1(demultiplexer_1_out1), .out2(demultiplexer_1_out2),
    .out3(demultiplexer_1_out3), .out4(demultiplexer_1_out4), .out5(demultiplexer_1_out5),
    .out6(demultiplexer_1_out6), .out7(demultiplexer_1_out7), .in(Reg_WE), .sel(rd));  // open: en
  Register #(.width(16)) register_1 (.D(REG_rd), .en(demultiplexer_1_out1), .Q(register_1_q), .clk(CLK));  // open: clr
  Register #(.width(16)) register_2 (.D(REG_rd), .en(demultiplexer_1_out2), .Q(register_2_q), .clk(CLK));  // open: clr
  Register #(.width(16)) register_3 (.D(REG_rd), .en(demultiplexer_1_out3), .Q(register_3_q), .clk(CLK));  // open: clr
  Register #(.width(16)) register_4 (.D(REG_rd), .en(demultiplexer_1_out4), .Q(register_4_q), .clk(CLK));  // open: clr
  Register #(.width(16)) register_5 (.D(REG_rd), .en(demultiplexer_1_out5), .Q(register_5_q), .clk(CLK));  // open: clr
  Register #(.width(16)) register_6 (.D(REG_rd), .en(demultiplexer_1_out6), .Q(register_6_q), .clk(CLK));  // open: clr
  Register #(.width(16)) register_7 (.D(REG_rd), .en(demultiplexer_1_out7), .Q(register_7_q), .clk(CLK));  // open: clr
  Multiplexer #(.select(3), .width(16)) multiplexer_1 (
    .in0({16{1'b0}}), .in1(register_1_q), .in2(register_2_q), .in3(register_3_q), .in4(register_4_q),
    .in5(register_5_q), .in6(register_6_q), .in7(register_7_q), .out(REG_rs), .sel(rs));  // open: en
  // Probe on REG_rs
  // Probe on REG_rt
  Multiplexer #(.select(3), .width(16)) multiplexer_2 (
    .in0({16{1'b0}}), .in1(register_1_q), .in2(register_2_q), .in3(register_3_q), .in4(register_4_q),
    .in5(register_5_q), .in6(register_6_q), .in7(register_7_q), .out(REG_rt), .sel(rt));  // open: en
  // also tied to GND on the sheet: demultiplexer_1_out0
endmodule

module PC_FSM (
  input  [15:0] Offset,
  input  [15:0] Target,
  input  [15:0] Reg_rs,
  input  [15:0] Reg_rt,
  input  Jump,
  input  [1:0] Branch,
  input  isBranch,
  input  Halt,
  input  CLK,
  output [7:0] PC_Out,
  output [15:0] PC_1_Out
);

  wire branchCtrl, multiplexer_3_out, not_1_out, not_2_out, or_1_out, tunnel, tunnel_t, tunnel_t_t;
  wire [7:0] adder_1_out, bit_extender_1_out, bit_extender_2_out, multiplexer_1_out, multiplexer_2_out;

  Bit_Extender #(.in_width(16), .out_width(8)) bit_extender_1 (.in(Offset), .out(bit_extender_1_out));
  Adder adder_1 (.a(PC_Out), .b(multiplexer_1_out), .out(adder_1_out));  // open: cin, cout
  Multiplexer #(.width(8)) multiplexer_1 (
    .in0(8'h1), .in1(bit_extender_1_out), .out(multiplexer_1_out), .sel(branchCtrl));  // open: en
  Bit_Extender #(.in_width(16), .out_width(8)) bit_extender_2 (.in(Target), .out(bit_extender_2_out));
  assign PC_1_Out = {{8{1'b0}}, adder_1_out};  // Bit_Extender bit_extender_3
  Multiplexer #(.width(8)) multiplexer_2 (
    .in0(adder_1_out), .in1(bit_extender_2_out), .out(multiplexer_2_out), .sel(Jump));  // open: en
  not not_1 (not_1_out, Halt);
  Comparator #(.width(16)) comparator_1 (.a(Reg_rs), .b(Reg_rt), .gt(tunnel_t_t), .eq(tunnel_t), .lt(tunnel));
  Register PC (.D(multiplexer_2_out), .en(not_1_out), .Q(PC_Out), .clk(CLK));  // open: clr
  or or_1 (or_1_out, tunnel_t_t, tunnel_t);
  Multiplexer #(.select(2)) multiplexer_3 (
    .in0(tunnel), .in1(or_1_out), .in2(tunnel_t), .in3(not_2_out), .out(multiplexer_3_out), .sel(Branch));  // open: en
  not not_2 (not_2_out, tunnel_t);
  and and_1 (branchCtrl, multiplexer_3_out, isBranch);

  // Other names for the same wires on the sheet: Is_Branch = isBranch; PC__1_Out[15:0] = PC_1_Out;
  //   Reg_rst[15:0] = Reg_rt
endmodule

module Control (
  input  [21:0] Instruction,
  output [1:0] BranchOp,
  output [2:0] rd,
  output RegWE,
  output [2:0] rs,
  output [2:0] rt,
  output [2:0] RegDataSrc,
  output hlt,
  output MemWE,
  output DispWE,
  output [15:0] imm,
  output ALUBSrc,
  output Jump,
  output [2:0] ALUOP,
  output is_Branch,
  output jr
);

  wire add, adi, \and , ani, beq, bge, blt, bne, j, jal, ld, li, lui, mov, \not , \or , or_5_out, or_6_out,
       or_7_out, or_8_out, or_9_out, or_10_out, or_11_out, ori, sbi, shl, shr, sli, sri, sub, undriven,
       \xor , xri;
  wire [15:0] bit_extender_1_out, bit_extender_2_out;

  // Probe on imm
  or or_1 (Jump, jr, jal, j);
  or or_2 (is_Branch, bge, blt, beq, bne);
  Decoder #(.select(5)) decoder_1 (
    .out0(hlt), .out1(DispWE), .out2(li), .out3(lui), .out4(mov), .out5(ld), .out6(MemWE), .out7(add),
    .out8(sub), .out9(\and ), .out10(\or ), .out11(\xor ), .out12(\not ), .out13(shl), .out14(shr),
    .out15(adi), .out16(sbi), .out17(ani), .out18(ori), .out19(xri), .out20(sli), .out21(sri), .out22(j),
    .out23(blt), .out24(bge), .out25(beq), .out26(bne), .out27(jal), .out28(jr), .sel(Instruction[21:17]));  // open: out29, out30, out31, en
  or or_3 (RegWE, li, lui, mov, ld, add, sub, \and , \or , \xor , \not , shl, shr, adi, sbi, ani, ori, xri, sli, sri, jal);
  or or_4 (ALUBSrc, ld, adi, sbi, ani, ori, xri, sli, sri, MemWE);
  assign bit_extender_1_out = {{8{Instruction[16]}}, Instruction[16:9]};  // Bit_Extender bit_extender_1
  assign bit_extender_2_out = {{8{1'b0}}, Instruction[16:9]};  // Bit_Extender bit_extender_2
  Priority_Encoder priority_encoder_1 (
    .in0(1'b1), .in1(li), .in2(lui), .in3(ld), .in4(jal), .out(RegDataSrc));  // open: in5, in6, in7, en_in, gs, en_out
  Multiplexer #(.width(16)) multiplexer_1 (
    .in0(bit_extender_1_out), .in1(bit_extender_2_out), .out(imm), .sel(or_5_out));  // open: en
  or or_5 (or_5_out, ori, ani, xri, li);
  or or_6 (or_6_out, sub, sbi, \and );
  or or_7 (or_7_out, sbi, \and , ani);
  or or_8 (or_8_out, \or , ori, \xor );
  or or_9 (or_9_out, ori, \xor , xri);
  or or_10 (or_10_out, xri, undriven, shr);
  or or_11 (or_11_out, undriven, shr, sri);
  Priority_Encoder #(.select(2)) priority_encoder_2 (
    .in0(1'b1), .in1(bge), .in2(beq), .in3(bne), .out(BranchOp));  // open: gs, en_out, en_in
  Priority_Encoder priority_encoder_3 (
    .in0(1'b1), .in1(or_6_out), .in2(or_7_out), .in3(or_8_out), .in4(or_9_out), .in5(\not ), .in6(or_10_out),
    .in7(or_11_out), .out(ALUOP));  // open: en_in, gs, en_out

  assign rd = Instruction[8:6];
  assign rs = Instruction[5:3];
  assign rt = Instruction[2:0];

  // Other names for the same wires on the sheet: Imm8[7:0] = Instruction[16:9]; put = DispWE; st = MemWE
endmodule
