// Logisim project cjm235lab5.circ as structural Verilog: 1 circuit, main circuit main
module main (
  input  [3:0] A,
  input  [3:0] B,
  input  sub
);

  wire and_1_out, and_2_out, Co, not_2_out, not_3_out, not_4_out, SOV, UOV;
  wire [3:0] not_1_out, O, Sb;

  xor xor_1 (UOV, Co, sub);
  assign not_1_out = ~B;  // NOT_Gate not_1, 4 bits wide
  // Probe on Sb
  // Probe on A
  // Probe on A
  // Probe on B
  // Probe on B
  // Probe on O
  // Probe on O
  LED led_1 (.in(UOV));
  LED led_2 (.in(SOV));
  Multiplexer #(.width(4)) multiplexer_1 (.in0(B), .in1(not_1_out), .out(Sb), .sel(sub));  // open: en
  // Probe on Co
  // Probe on O
  Adder #(.width(4)) adder_1 (.a(A), .b(Sb), .out(O), .cin(sub), .cout(Co));
  // NOT_Gate not_2 has open pins: in=open, out=not_2_out
  // NOT_Gate not_3 has open pins: in=open, out=not_3_out
  // NOT_Gate not_4 has open pins: in=open, out=not_4_out
  and and_1 (and_1_out, not_2_out, not_3_out, O[3]);
  or or_1 (SOV, and_1_out, and_2_out);
  and and_2 (and_2_out, A[3], Sb[3], not_4_out);
endmodule
