// Logisim project register_file.circ as structural Verilog: 2 circuits, main circuit main
module main (
  input  [7:0] REG_rd,
  input  WE,
  input  [1:0] rd,
  input  [1:0] rs,
  input  [1:0] rt
);

  wire button_1_out, Clk, clock_1_out, demultiplexer_1_out0, demultiplexer_1_out1, demultiplexer_1_out2,
       demultiplexer_1_out3;
  wire [7:0] _1__at_q, _2__V0_q, _3__v1_q, multiplexer_1_out, multiplexer_2_out;

  Clock clock_1 (.out(clock_1_out));
  Button button_1 (.out(button_1_out));
  or or_1 (Clk, clock_1_out, button_1_out);
  Demultiplexer #(.select(2)) demultiplexer_1 (
    .out0(demultiplexer_1_out0), .out1(demultiplexer_1_out1), .out2(demultiplexer_1_out2),
    .out3(demultiplexer_1_out3), .in(WE), .sel(rd));  // open: en
  // Probe on REG_rd
  Register _1__at (.D(REG_rd), .en(demultiplexer_1_out1), .Q(_1__at_q), .clk(Clk));  // open: clr
  Register _2__V0 (.D(REG_rd), .en(demultiplexer_1_out2), .Q(_2__V0_q), .clk(Clk));  // open: clr
  Register _3__v1 (.D(REG_rd), .en(demultiplexer_1_out3), .Q(_3__v1_q), .clk(Clk));  // open: clr
  // Probe on multiplexer_1_out
  Multiplexer #(.select(2), .width(8)) multiplexer_1 (
    .in0({8{1'b0}}), .in1(_1__at_q), .in2(_2__V0_q), .in3(_3__v1_q), .out(multiplexer_1_out), .sel(rs));  // open: en
  // Probe on multiplexer_2_out
  Multiplexer #(.select(2), .width(8)) multiplexer_2 (
    .in0({8{1'b0}}), .in1(_1__at_q), .in2(_2__V0_q), .in3(_3__v1_q), .out(multiplexer_2_out), .sel(rt));  // open: en
endmodule

module Register_File (
  input  [7:0] REG_rd,
  input  WE,
  input  [1:0] rd,
  input  [1:0] rs,
  input  [1:0] rt
);

  wire Clk, demultiplexer_1_out0, demultiplexer_1_out1, demultiplexer_1_out2, demultiplexer_1_out3;
  wire [7:0] _1__at_q, _2__V0_q, _3__v1_q, multiplexer_1_out, multiplexer_2_out;

  Demultiplexer #(.select(2)) demultiplexer_1 (
    .out0(demultiplexer_1_out0), .out1(demultiplexer_1_out1), .out2(demultiplexer_1_out2),
    .out3(demultiplexer_1_out3), .in(WE), .sel(rd));  // open: en
  // Probe on REG_rd
  Register _1__at (.D(REG_rd), .en(demultiplexer_1_out1), .Q(_1__at_q), .clk(Clk));  // open: clr
  Register _2__V0 (.D(REG_rd), .en(demultiplexer_1_out2), .Q(_2__V0_q), .clk(Clk));  // open: clr
  Register _3__v1 (.D(REG_rd), .en(demultiplexer_1_out3), .Q(_3__v1_q), .clk(Clk));  // open: clr
  // Probe on multiplexer_1_out
  Multiplexer #(.select(2), .width(8)) multiplexer_1 (
    .in0({8{1'b0}}), .in1(_1__at_q), .in2(_2__V0_q), .in3(_3__v1_q), .out(multiplexer_1_out), .sel(rs));  // open: en
  Multiplexer #(.select(2), .width(8)) multiplexer_2 (
    .in0({8{1'b0}}), .in1(_1__at_q), .in2(_2__V0_q), .in3(_3__v1_q), .out(multiplexer_2_out), .sel(rt));  // open: en
  // Probe on multiplexer_2_out
endmodule
