// Logisim project splitter_bitfields.circ as structural Verilog: 1 circuit, main circuit main
module main (
  input  [31:0] I_type,
  input  [15:0] imm,
  input  [4:0] rt,
  input  [4:0] rs,
  input  [5:0] opcode
);

  // Probe on I_type[15:0]
  // Probe on I_type[20:16]
  // Probe on I_type[25:21]
  // Probe on I_type[31:26]
  // Probe on {opcode, rs, rt, imm}

  // Notes on the sheet:
  //   It can be annoying with the dropdown boxes but
  //   don't forget you can copy and paste components.
  //   Bitfields are really easy in hardware!
  //   ^^^ Check out the "Bit 0..Bit31" properties here.
  //   Works for putting them together too.
endmodule
