// Logisim project splitter_tricks.circ as structural Verilog: 1 circuit, main circuit main
module main (
  input  [1:0] in_1,
  input  [7:0] in_2,
  input  [7:0] in_3
);

  // Probe on {in_1[0], in_1[1]}
  // Probe on in_3[7]
  // Probe on in_2[3:0]
  // Probe on in_2[7:4]

  // Notes on the sheet:
  //   Try changing the appearance.
  //   They all do the same thing, but might fit better.
  //   "Bit Width In" controls how many bits are on the combined end.
  //   "Fan Out" controls how many values the combined value is split into.
  //   A "Fan Out" of 1 is great for extracting a single value or bit.
  //   "Centered" is smallest.
  //   Select it and use the arrow keys to change direction.
  //   Set the bits you don't care about to "None."
  //   You can change the order of the bits, too.
endmodule
