// Logisim project tunnel_tutorial.circ as structural Verilog: 2 circuits, main circuit main
module main (
  input  A,
  input  B,
  input  C,
  input  is_there_a_dog,
  input  is_there_a_cat
);

  wire and_1_out, CK, pet_it, should_light;
  wire [16:0] display_logic_1_out_2, display_logic_1_out_3, display_logic_1_out_4, display_logic_1_out_5,
       display_logic_1_out_6;

  Clock clock_1 (.out(CK));
  Register u_a (.clk(CK));  // open: D, en, Q, clr
  and and_1 (and_1_out, ~A, B);  // AND_Gate
  or or_1 (should_light, and_1_out, ~C);  // OR_Gate
  Display_Logic display_logic_1 (
    .pet(pet_it), .out_2(display_logic_1_out_2), .out_3(display_logic_1_out_3),
    .out_4(display_logic_1_out_4), .out_5(display_logic_1_out_5), .out_6(display_logic_1_out_6));
  DotMatrix #(.inputtype("row"), .matrixcols(17), .matrixrows(5)) dotmatrix_1 (
    .row0(display_logic_1_out_2), .row1(display_logic_1_out_3), .row2(display_logic_1_out_4),
    .row3(display_logic_1_out_5), .row4(display_logic_1_out_6));
  Register u_b (.clk(CK));  // open: D, en, Q, clr
  Register u_c (.clk(CK));  // open: D, en, Q, clr
  Register d (.clk(CK));  // open: D, en, Q, clr
  LED led_1 (.in(should_light));
  or or_2 (pet_it, is_there_a_dog, is_there_a_cat);

  // Other names for the same wires on the sheet: cat_nearby = is_there_a_cat; dog_nearby = is_there_a_dog

  // Notes on the sheet:
  //   Tunnels are really useful.
  //   They let you arrange your circuit any way you want.
  //   For wires that have to go to many places,
  //   tunnels make your circuits much cleaner.
  //   They let you give wires names,
  //   so that you're not wondering "what's this for?"
  //   They make your logic easier to read.
endmodule

// magic!
module Display_Logic (
  input  pet,
  output [16:0] out_2,
  output [16:0] out_3,
  output [16:0] out_4,
  output [16:0] out_5,
  output [16:0] out_6
);

  Multiplexer #(.width(17), .enable("false")) multiplexer_1 (.in0(17'h22f4), .in1(17'h1ef7d), .out(out_2), .sel(pet));
  Multiplexer #(.width(17), .enable("false")) multiplexer_2 (.in0(17'h3294), .in1(17'h12811), .out(out_3), .sel(pet));
  Multiplexer #(.width(17), .enable("false")) multiplexer_3 (.in0(17'h2a94), .in1(17'h1ef11), .out(out_4), .sel(pet));
  Multiplexer #(.width(17), .enable("false")) multiplexer_4 (.in0(17'h2690), .in1(17'h10810), .out(out_5), .sel(pet));
  Multiplexer #(.width(17), .enable("false")) multiplexer_5 (.in0(17'h22f4), .in1(17'h10f11), .out(out_6), .sel(pet));

  // Notes on the sheet:
  //   yeah, I didn't use tunnels, SO WHAT
endmodule
